# Fritzing sketch Mbedded_sketch (saved by Fritzing 0.7.10b)

parts:
  Arduino_LiliyPad1 = Arduino LilyPad
  J1 = Basic Force Sensing Resistor (FSR) [package=THT]
  R1 = Resistor [tolerance=±5% resistance=10k package=THT]

nets:
  N1: Arduino_LiliyPad1.GND, J1.pin_1
  N2: Arduino_LiliyPad1.POW, R1.Pin_1
  N3: Arduino_LiliyPad1.A0, J1.pin_0, R1.Pin_0
